# Fritzing sketch ap_schematic (saved by Fritzing 0.9.3b)
breadboards: 1

parts:
  R1 = Resistor [tolerance=±5% resistance=100 package=THT]
  R3 = Resistor [tolerance=±5% resistance=100 package=THT]
  R2 = Resistor [tolerance=±5% resistance=100 package=THT]
  Grow_LED_2 = LED - 5mm [color="White (4500K)" package="5 mm [THT]"]
  Grow_LED_3 = LED - 5mm [color="White (4500K)" package="5 mm [THT]"]
  LED_Transistor = NPN-Transistor [part_number=2N2222A package="TO92 [THT]"]
  Grow_LED_1 = smd LED [color="White (4500K)" package="0603 [SMD]"]
  C1 = Tantalum Capacitor [capacitance=1μF package="100 mil [THT, tantalum]"]
  D1 = Rectifier Diode [part_number=1N4001 package="300 mil [THT]"]
  M1 = DC Motor
  Pump_MOSFET = Basic FET N-Channel [part_number=AO3400 package="DPak [SMD]"]
  R4 = Resistor [tolerance=±5% resistance=10k package=THT]
  Nano = Arduino Nano (Rev3.0)
  R5 = Resistor [tolerance=±5% resistance=1k package=THT]
  Part1 = Soil Moisture Sensor

nets (from the schematic view):
  N1: R1.Pin_0, Grow_LED_1.cathode
  N2: R1.Pin_1, R3.Pin_1, R2.Pin_1, LED_Transistor.C
  N3: R3.Pin_0, Grow_LED_3.cathode
  N4: R2.Pin_0, Grow_LED_2.cathode
  5V: Grow_LED_2.anode, Grow_LED_3.anode, Grow_LED_1.anode, C1.+, D1.anode, M1.pin_1, Part1.VCC
  GND: LED_Transistor.E, Pump_MOSFET.drain, Nano.GND, Part1.GND
  N5: LED_Transistor.B, R5.Pin_0
  N6: C1.-, D1.cathode, M1.pin_2, Pump_MOSFET.source
  N7: Pump_MOSFET.Gate, R4.Pin_1
  N8: R4.Pin_0, Nano.D2
  N9: Nano.D3, R5.Pin_1
  N10: Nano.A0, Part1.SIG
